# Fritzing sketch Untitled Sketch (saved by Fritzing 1.0.1rc)
stripboards: 1

parts:
  Composant1 = Arduino Uno (Rev3)
  R1 = Resistor [tolerance=±5% power=0.25W resistance=220 package=THT]
  LED1 = LED - 5mm [color="Red (633nm)" current=0.030A package="5 mm [THT]"]

nets (from the breadboard view):
  N1: Composant1.D13/SCK, R1.Pin_1
  N2: Composant1.GND, LED1.cathode
  N3: R1.Pin_0, LED1.anode
