# Fritzing sketch Electronic_part (saved by Fritzing 1.0.1rc)
stripboards: 1

parts:
  Composant1 = 24 NeoPixel Ring [part_number=1586]
  Composant2 = Adafruit MicroLipo Charger USB Type C [part_number="Adafruit #4410"]
  U1 = LIPO-2000mAh [package=lipo-2000]
  Composant3 = Arduino Nano 33 BLE Sense
  J1 = Piezo Speaker

nets:
  N1: Composant1.IN, Composant3.D3~
  VDD: Composant1.VDD, Composant3.3V3
  GND: Composant1.GND, Composant2.GND, U1.-, Composant3.GND, Composant3.A7, J1.pin1
  N2: Composant2.VBAT, U1.+
  5V: Composant2.5V, Composant3.VIN
  N3: Composant3.D9~, J1.pin2

custom parts:
  24 NeoPixel Ring: 24 ultra bright smart LED NeoPixels are arranged in a circle with 2.6" (66mm) outer diameter. The rings are 'chainable' - connect the output pin of one to the input pin of another. Use only one microcontroller pin to control as many as you can chain together! Each LED is addressable as the driver chip is inside the LED. Each one has ~18mA constant current drive so the color will be very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
  Adafruit MicroLipo Charger USB Type C: Oh so handy, this little lipo charger is so small and easy to use you can keep it on your desk or mount it easily into any project! Simply plug it via any USB C cable into a USB port and a 3.7V/4.2V lithium polymer or lithium ion rechargeable battery into the JST plug on the other end. There are two LEDs - one red and one green. While charging, the red LED is lit. When the battery is fully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
  Arduino Nano 33 BLE Sense: The Nano 33 BLE Sense (without headers) is Arduino’s 3.3V AI enabled board in the smallest available form factor: 45x18mm! The Arduino Nano 33 BLE Sense is a completely new board on a well-known form factor. It comes with a series of embedded sensors: 9 axis inertial sensor: what makes this board ideal for wearable devices humidity, and temperature sensor: to get highly accurate measurements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
